// Logisim project Lab1_Part1_demo.circ as structural Verilog: 1 circuit, main circuit main
module main (
  input  x,
  input  s,
  input  y,
  output f
);

  wire and_1_out, not_1_out, or_1_out;

  not not_1 (not_1_out, s);
  and and_1 (and_1_out, x, not_1_out);
  or or_1 (or_1_out, s, y);
  or or_2 (f, and_1_out, or_1_out);
endmodule
