// Logisim project Lab1_Part2_demo.circ as structural Verilog: 2 circuits, main circuit main
module main (
  input  a,
  input  b,
  input  c,
  output f
);

  wire and_1_out, not_1_out, not_2_out, or_1_out;

  not not_1 (not_1_out, b);
  or or_1 (or_1_out, a, b);
  and and_1 (and_1_out, not_1_out, c);
  not not_2 (not_2_out, or_1_out);
  or or_2 (f, not_2_out, and_1_out);
endmodule

module Lab1_Part2_2 (
  input  a,
  input  c,
  input  b,
  output f
);

  wire not_1_out, not_2_out, or_1_out;

  not not_1 (not_1_out, a);
  or or_1 (or_1_out, not_1_out, c);
  not not_2 (not_2_out, b);
  and and_1 (f, or_1_out, not_2_out);
endmodule
