// Logisim project mux.circ as structural Verilog: 4 circuits, main circuit main
module main (
  input  SW_0,
  input  SW_1,
  input  SW_9,
  output LEDR_9
);

  mux2to1 u (.x(SW_0), .y(SW_1), .s(SW_9), .m(LEDR_9));
endmodule

module mux2to1 (
  input  x,
  input  y,
  input  s,
  output m
);

  Multiplexer #(.enable("false")) multiplexer_1 (.in0(x), .in1(y), .out(m), .sel(s));
endmodule

module Components (
  input  u,
  input  v,
  input  s_0,
  input  w,
  input  x,
  input  s_1,
  output m
);

  wire a_m, b_m;

  mux2to1 a (.x(u), .y(v), .s(s_0), .m(a_m));
  mux2to1 b (.x(w), .y(x), .s(s_0), .m(b_m));
  mux2to1 c (.x(a_m), .y(b_m), .s(s_1), .m(m));
endmodule

module DE1 (
  input  SW_0,
  input  SW_1,
  input  SW_2,
  input  SW_3,
  input  SW_8,
  input  SW_9,
  output LEDR_0
);

  Components components_1 (.u(SW_0), .v(SW_1), .s_0(SW_8), .w(SW_2), .x(SW_3), .s_1(SW_9), .m(LEDR_0));
endmodule
