// Logisim project lab3part2.circ as structural Verilog: 2 circuits, main circuit main
module main (
  input  c_in,
  input  [3:0] A,
  input  [3:0] B,
  output [3:0] LEDR,
  output c_out
);

  wire fa_1_c_0, fa_2_c_0, fa_3_c_0;

  FA fa_1 (.c_i(c_in), .a(A[0]), .b(B[0]), .s(LEDR[0]), .c_0(fa_1_c_0));
  FA fa_2 (.c_i(fa_1_c_0), .a(A[1]), .b(B[1]), .s(LEDR[1]), .c_0(fa_2_c_0));
  FA fa_3 (.c_i(fa_2_c_0), .a(A[2]), .b(B[2]), .s(LEDR[2]), .c_0(fa_3_c_0));
  FA fa_4 (.c_i(fa_3_c_0), .a(A[3]), .b(B[3]), .s(LEDR[3]), .c_0(c_out));
endmodule

module FA (
  input  c_i,
  input  a,
  input  b,
  output s,
  output c_0
);

  wire xor_1_out;

  xor xor_1 (xor_1_out, a, b);
  Multiplexer #(.enable("false")) multiplexer_1 (.in0(b), .in1(c_i), .out(c_0), .sel(xor_1_out));
  xor xor_2 (s, c_i, xor_1_out);
endmodule
