// Logisim project lab3part3.circ as structural Verilog: 18 circuits, main circuit ALU
module ripple_carry_adder (
  input  c_in,
  input  [3:0] A,
  input  [3:0] B,
  output [3:0] LEDR,
  output c_out
);

  wire fa_1_c_0, fa_2_c_0, fa_3_c_0;

  FA fa_1 (.c_i(c_in), .a(A[0]), .b(B[0]), .s(LEDR[0]), .c_0(fa_1_c_0));
  FA fa_2 (.c_i(fa_1_c_0), .a(A[1]), .b(B[1]), .s(LEDR[1]), .c_0(fa_2_c_0));
  FA fa_3 (.c_i(fa_2_c_0), .a(A[2]), .b(B[2]), .s(LEDR[2]), .c_0(fa_3_c_0));
  FA fa_4 (.c_i(fa_3_c_0), .a(A[3]), .b(B[3]), .s(LEDR[3]), .c_0(c_out));
endmodule

module FA (
  input  c_i,
  input  a,
  input  b,
  output s,
  output c_0
);

  wire xor_1_out;

  xor xor_1 (xor_1_out, a, b);
  Multiplexer #(.enable("false")) multiplexer_1 (.in0(b), .in1(c_i), .out(c_0), .sel(xor_1_out));
  xor xor_2 (s, c_i, xor_1_out);
endmodule

module Segment0 (
  input  c_3,
  input  c_2,
  input  c_1,
  input  c_0,
  output Hex0
);

  wire and_1_out, and_2_out, and_3_out, and_4_out, and_5_out, and_6_out, not_1_out, not_2_out, not_3_out,
       not_4_out, not_5_out;

  not not_1 (not_1_out, c_0);
  not not_2 (not_2_out, c_3);
  not not_3 (not_3_out, c_2);
  not not_4 (not_4_out, c_0);
  not not_5 (not_5_out, c_1);
  and and_1 (and_1_out, c_3, not_1_out);
  and and_2 (and_2_out, not_2_out, c_1);
  and and_3 (and_3_out, not_3_out, not_4_out);
  and and_4 (and_4_out, c_1, c_2);
  and and_5 (and_5_out, not_2_out, c_2, c_0);
  and and_6 (and_6_out, c_3, not_3_out, not_5_out);
  or or_1 (Hex0, and_1_out, and_2_out, and_3_out, and_4_out, and_5_out, and_6_out);
endmodule

module Segment1 (
  input  c_3,
  input  c_2,
  input  c_1,
  input  c_0,
  output Hex1
);

  wire and_1_out, and_2_out, and_3_out, and_4_out, and_5_out, not_1_out, not_2_out, not_3_out, not_4_out;

  not not_1 (not_1_out, c_3);
  not not_2 (not_2_out, c_2);
  not not_3 (not_3_out, c_1);
  not not_4 (not_4_out, c_0);
  and and_1 (and_1_out, not_2_out, not_4_out);
  and and_2 (and_2_out, not_1_out, not_2_out);
  and and_3 (and_3_out, not_1_out, not_3_out, not_4_out);
  and and_4 (and_4_out, c_3, not_3_out, c_0);
  and and_5 (and_5_out, not_1_out, c_1, c_0);
  or or_1 (Hex1, and_1_out, and_2_out, and_3_out, and_4_out, and_5_out);
endmodule

module Segment2 (
  input  c_3,
  input  c_2,
  input  c_1,
  input  c_0,
  output Hex2
);

  wire and_1_out, and_2_out, and_3_out, and_4_out, and_5_out, not_1_out, not_2_out, not_3_out;

  not not_1 (not_1_out, c_3);
  not not_2 (not_2_out, c_2);
  not not_3 (not_3_out, c_1);
  and and_1 (and_1_out, not_1_out, not_3_out);
  and and_2 (and_2_out, not_1_out, c_0);
  and and_3 (and_3_out, c_3, not_2_out);
  and and_4 (and_4_out, not_1_out, c_2);
  and and_5 (and_5_out, not_3_out, c_0);
  or or_1 (Hex2, and_1_out, and_2_out, and_3_out, and_4_out, and_5_out);
endmodule

module Segment3 (
  input  c_3,
  input  c_2,
  input  c_1,
  input  c_0,
  output Hex3
);

  wire and_1_out, and_2_out, and_3_out, and_4_out, and_5_out, not_1_out, not_2_out, not_3_out, not_4_out;

  not not_1 (not_1_out, c_3);
  not not_2 (not_2_out, c_2);
  not not_3 (not_3_out, c_1);
  not not_4 (not_4_out, c_0);
  and and_1 (and_1_out, not_1_out, not_2_out, not_4_out);
  and and_2 (and_2_out, c_3, not_3_out, not_4_out);
  and and_3 (and_3_out, c_2, not_3_out, c_0);
  and and_4 (and_4_out, not_2_out, c_1, c_0);
  and and_5 (and_5_out, c_2, c_1, not_4_out);
  or or_1 (Hex3, and_1_out, and_2_out, and_3_out, and_4_out, and_5_out);
endmodule

module Segment4 (
  input  c_3,
  input  c_2,
  input  c_1,
  input  c_0,
  output Hex4
);

  wire and_1_out, and_2_out, and_3_out, and_4_out, not_1_out, not_2_out;

  not not_1 (not_1_out, c_2);
  not not_2 (not_2_out, c_0);
  and and_1 (and_1_out, c_3, c_2);
  and and_2 (and_2_out, c_1, not_2_out);
  and and_3 (and_3_out, not_1_out, not_2_out);
  and and_4 (and_4_out, c_3, c_1);
  or or_1 (Hex4, and_1_out, and_2_out, and_3_out, and_4_out);
endmodule

module Segment5 (
  input  c_3,
  input  c_2,
  input  c_1,
  input  c_0,
  output Hex5
);

  wire and_1_out, and_2_out, and_3_out, and_4_out, and_5_out, not_1_out, not_2_out, not_3_out, not_4_out;

  not not_1 (not_1_out, c_3);
  not not_2 (not_2_out, c_2);
  not not_3 (not_3_out, c_1);
  not not_4 (not_4_out, c_0);
  and and_1 (and_1_out, not_3_out, not_4_out);
  and and_2 (and_2_out, c_3, not_2_out);
  and and_3 (and_3_out, not_1_out, c_2, not_3_out);
  and and_4 (and_4_out, c_3, c_2, c_1);
  and and_5 (and_5_out, c_2, c_1, not_4_out);
  or or_1 (Hex5, and_1_out, and_2_out, and_3_out, and_4_out, and_5_out);
endmodule

module Segment6 (
  input  c_3,
  input  c_2,
  input  c_1,
  input  c_0,
  output Hex6
);

  wire and_1_out, and_2_out, and_3_out, and_4_out, and_5_out, and_6_out, not_1_out, not_2_out, not_3_out,
       not_4_out;

  not not_1 (not_1_out, c_3);
  not not_2 (not_2_out, c_2);
  not not_3 (not_3_out, c_1);
  not not_4 (not_4_out, c_0);
  and and_1 (and_1_out, c_3, not_2_out);
  and and_2 (and_2_out, c_1, not_4_out);
  and and_3 (and_3_out, c_3, c_0);
  and and_4 (and_4_out, c_3, c_1);
  and and_5 (and_5_out, not_1_out, c_2, not_3_out);
  and and_6 (and_6_out, not_1_out, not_2_out, c_1);
  or or_1 (Hex6, and_1_out, and_2_out, and_3_out, and_4_out, and_5_out, and_6_out);
endmodule

module Display (
  input  SW_3,
  input  SW_2,
  input  SW_1,
  input  SW_0,
  output S0,
  output S1,
  output S2,
  output S3,
  output S4,
  output S5,
  output S6
);

  Segment0 Hex0 (.c_3(SW_3), .c_2(SW_2), .c_1(SW_1), .c_0(SW_0), .Hex0(S0));
  Segment1 Hex1 (.c_3(SW_3), .c_2(SW_2), .c_1(SW_1), .c_0(SW_0), .Hex1(S1));
  Segment2 Hex2 (.c_3(SW_3), .c_2(SW_2), .c_1(SW_1), .c_0(SW_0), .Hex2(S2));
  Segment3 Hex3 (.c_3(SW_3), .c_2(SW_2), .c_1(SW_1), .c_0(SW_0), .Hex3(S3));
  Segment4 Hex4 (.c_3(SW_3), .c_2(SW_2), .c_1(SW_1), .c_0(SW_0), .Hex4(S4));
  Segment5 Hex5 (.c_3(SW_3), .c_2(SW_2), .c_1(SW_1), .c_0(SW_0), .Hex5(S5));
  Segment6 Hex6 (.c_3(SW_3), .c_2(SW_2), .c_1(SW_1), .c_0(SW_0), .Hex6(S6));
endmodule

module ALU (
  input  [3:0] A,
  input  [3:0] B,
  input  [2:0] F,
  output [7:0] ALUout
);

  wire [7:0] function0_1_aluout, function1_1_aluout, function2_1_aluout, function3_1_aluout,
       function4_1_aluout, function5_1_aluout;

  function0 function0_1 (.A(A), .ALUout(function0_1_aluout));
  function1 function1_1 (.A(A), .B(B), .ALUout(function1_1_aluout));
  function2 function2_1 (.A(A), .B(B), .ALUout(function2_1_aluout));
  function3 function3_1 (.A(A), .B(B), .ALUout(function3_1_aluout));
  function4 function4_1 (.A(A), .B(B), .ALUout(function4_1_aluout));
  function5 function5_1 (.A(A), .B(B), .ALUout(function5_1_aluout));
  Multiplexer #(.enable("false"), .select(3), .width(8)) multiplexer_1 (
    .in0(function0_1_aluout), .in1(function1_1_aluout), .in2(function2_1_aluout), .in3(function3_1_aluout),
    .in4(function4_1_aluout), .in5(function5_1_aluout), .out(ALUout), .sel(F));  // open: in6, in7
endmodule

module function0 (
  input  [3:0] A,
  output [7:0] ALUout
);

  wire ripple_carry_adder_1_c_out;

  ripple_carry_adder ripple_carry_adder_1 (
    .c_in(1'b1), .A(A), .B(4'b0000), .LEDR(ALUout[3:0]), .c_out(ripple_carry_adder_1_c_out));
  assign ALUout[7:4] = {{3{1'b0}}, ripple_carry_adder_1_c_out};  // Bit_Extender bit_extender_1
endmodule

module function1 (
  input  [3:0] A,
  input  [3:0] B,
  output [7:0] ALUout
);

  wire ripple_carry_adder_1_c_out;

  ripple_carry_adder ripple_carry_adder_1 (
    .c_in(1'b0), .A(A), .B(B), .LEDR(ALUout[3:0]), .c_out(ripple_carry_adder_1_c_out));
  assign ALUout[7:4] = {{3{1'b0}}, ripple_carry_adder_1_c_out};  // Bit_Extender bit_extender_1
endmodule

module function2 (
  input  [3:0] A,
  input  [3:0] B,
  output [7:0] ALUout
);

  wire adder_1_cout;

  Adder #(.width(4)) adder_1 (.a(A), .b(B), .out(ALUout[3:0]), .cin(1'b0), .cout(adder_1_cout));
  assign ALUout[7:4] = {{3{1'b0}}, adder_1_cout};  // Bit_Extender bit_extender_1
endmodule

module function3 (
  input  [3:0] A,
  input  [3:0] B,
  output [7:0] ALUout
);

  assign ALUout[3:0] = A ^ B;  // XOR_Gate xor_1, 4 bits wide
  assign ALUout[7:4] = A | B;  // OR_Gate or_1, 4 bits wide
endmodule

module function4 (
  input  [3:0] A,
  input  [3:0] B,
  output [7:0] ALUout
);

  wire or_1_out;

  or or_1 (or_1_out, A[0], A[1], A[2], A[3], B[0], B[1], B[2], B[3]);
  assign ALUout = {{7{1'b0}}, or_1_out};  // Bit_Extender bit_extender_1
endmodule

module function5 (
  input  [3:0] A,
  input  [3:0] B,
  output [7:0] ALUout
);


  assign ALUout = {A, B};
endmodule

module main (
  input  [3:0] A,
  input  [3:0] B,
  input  [2:0] F,
  output [7:0] ALUout
);

  wire display_1_s0, display_1_s1, display_1_s2, display_1_s3, display_1_s4, display_1_s5, display_1_s6,
       display_2_s0, display_2_s1, display_2_s2, display_2_s3, display_2_s4, display_2_s5, display_2_s6;

  ALU alu_1 (.A(A), .B(B), .F(F), .ALUout(ALUout));
  Display display_1 (
    .SW_3(ALUout[3]), .SW_2(ALUout[2]), .SW_1(ALUout[1]), .SW_0(ALUout[0]), .S0(display_1_s0),
    .S1(display_1_s1), .S2(display_1_s2), .S3(display_1_s3), .S4(display_1_s4), .S5(display_1_s5),
    .S6(display_1_s6));
  Display display_2 (
    .SW_3(ALUout[7]), .SW_2(ALUout[6]), .SW_1(ALUout[5]), .SW_0(ALUout[4]), .S0(display_2_s0),
    .S1(display_2_s1), .S2(display_2_s2), .S3(display_2_s3), .S4(display_2_s4), .S5(display_2_s5),
    .S6(display_2_s6));
  _7_Segment_Display u_7_segment_display_1 (
    .g(display_2_s6), .f(display_2_s5), .a(display_2_s0), .b(display_2_s1), .e(display_2_s4),
    .d(display_2_s3), .c(display_2_s2));  // open: dp
  _7_Segment_Display u_7_segment_display_2 (
    .g(display_1_s6), .f(display_1_s5), .a(display_1_s0), .b(display_1_s1), .e(display_1_s4),
    .d(display_1_s3), .c(display_1_s2));  // open: dp
endmodule
