// Logisim project lab4_part1.circ as structural Verilog
module D_latch (
  input  D,
  input  Clk,
  output Q_a,
  output Q_b
);

  wire nand_1_out, nand_2_out, not_1_out;

  not not_1 (not_1_out, D);
  nand nand_1 (nand_1_out, D, Clk);
  nand nand_2 (nand_2_out, Clk, not_1_out);
  nand nand_3 (Q_a, nand_1_out, Q_b);
  nand nand_4 (Q_b, Q_a, nand_2_out);
endmodule

module master_slave_flip_flop (
  input  D,
  input  Clk,
  output Q
);

  wire d_latch_1_q_a, not_1_out;

  not not_1 (not_1_out, Clk);
  D_latch d_latch_1 (.D(D), .Clk(Clk), .Q_a(d_latch_1_q_a));  // open: Q_b
  D_latch d_latch_2 (.D(d_latch_1_q_a), .Clk(not_1_out), .Q_a(Q));  // open: Q_b
endmodule
