// Logisim project lab4_part3.circ as structural Verilog: 4 circuits, main circuit main
module main (
  input  [7:0] LoadVal,
  input  ShiftRight,
  input  Load_n,
  input  clk,
  input  reset,
  input  ASR,
  output [7:0] Q
);

  ShifterRegister shifterregister_1 (
    .LoadVal(LoadVal), .ShiftRight(ShiftRight), .Load_n(Load_n), .clock(clk), .reset(reset), .ASR(ASR), .Q(Q));
endmodule

module mux2to1 (
  input  x,
  input  y,
  input  s,
  output m
);

  Multiplexer #(.enable("false")) multiplexer_1 (.in0(x), .in1(y), .out(m), .sel(s));
endmodule

module ShifterBit (
  input  load_val,
  input  in_val,
  input  shift,
  input  load_n,
  input  clk,
  input  reset,
  output out_val
);

  wire mux2to1_1_m, mux2to1_2_m;

  mux2to1 mux2to1_1 (.x(out_val), .y(in_val), .s(shift), .m(mux2to1_1_m));
  D_Flip_Flop d_ff_1 (.D(mux2to1_2_m), .clk(clk), .Q(out_val), .reset(reset));  // open: Qn, preset
  mux2to1 mux2to1_2 (.x(load_val), .y(mux2to1_1_m), .s(load_n), .m(mux2to1_2_m));
endmodule

module ShifterRegister (
  input  [7:0] LoadVal,
  input  ShiftRight,
  input  Load_n,
  input  clock,
  input  reset,
  input  ASR,
  output [7:0] Q
);

  wire mux2to1_1_m;

  mux2to1 mux2to1_1 (.x(1'b0), .y(LoadVal[7]), .s(ASR), .m(mux2to1_1_m));
  ShifterBit shifterbit_1 (
    .load_val(LoadVal[0]), .in_val(Q[1]), .shift(ShiftRight), .load_n(Load_n), .clk(clock), .reset(reset),
    .out_val(Q[0]));
  ShifterBit shifterbit_2 (
    .load_val(LoadVal[1]), .in_val(Q[2]), .shift(ShiftRight), .load_n(Load_n), .clk(clock), .reset(reset),
    .out_val(Q[1]));
  ShifterBit shifterbit_3 (
    .load_val(LoadVal[2]), .in_val(Q[3]), .shift(ShiftRight), .load_n(Load_n), .clk(clock), .reset(reset),
    .out_val(Q[2]));
  ShifterBit shifterbit_4 (
    .load_val(LoadVal[3]), .in_val(Q[4]), .shift(ShiftRight), .load_n(Load_n), .clk(clock), .reset(reset),
    .out_val(Q[3]));
  ShifterBit shifterbit_5 (
    .load_val(LoadVal[4]), .in_val(Q[5]), .shift(ShiftRight), .load_n(Load_n), .clk(clock), .reset(reset),
    .out_val(Q[4]));
  ShifterBit shifterbit_6 (
    .load_val(LoadVal[5]), .in_val(Q[6]), .shift(ShiftRight), .load_n(Load_n), .clk(clock), .reset(reset),
    .out_val(Q[5]));
  ShifterBit shifterbit_7 (
    .load_val(LoadVal[6]), .in_val(Q[7]), .shift(ShiftRight), .load_n(Load_n), .clk(clock), .reset(reset),
    .out_val(Q[6]));
  ShifterBit shifterbit_8 (
    .load_val(LoadVal[7]), .in_val(mux2to1_1_m), .shift(ShiftRight), .load_n(Load_n), .clk(clock),
    .reset(reset), .out_val(Q[7]));
endmodule
