// Logisim project lab7_part1.circ as structural Verilog: 9 circuits, main circuit main
module main (
  input  clear,
  input  enable,
  input  Switch
);

  wire and_1_out, Clk_out, display_1_s0, display_1_s1, display_1_s2, display_1_s3, display_1_s4,
       display_1_s5, display_1_s6, not_1_out, not_2_out, not_3_out, not_4_out, not_5_out, not_6_out,
       not_7_out;
  wire [3:0] counter_2_q, multiplexer_1_out, ram_1_dout;
  wire [5:0] counter_1_q;

  Clock Clk (.out(Clk_out));
  not not_1 (not_1_out, enable);
  Counter #(.max('h20), .ongoal("stay"), .width(6)) counter_1 (
    .clr(clear), .load(not_1_out), .up(1'b1), .clk(Clk_out), .D({6{1'b0}}), .Q(counter_1_q));  // open: count, carry
  Counter #(.max('hf), .width(4)) counter_2 (
    .clr(clear), .load(not_1_out), .up(1'b1), .clk(Clk_out), .D(4'b0000), .Q(counter_2_q));  // open: count, carry
  not not_2 (not_2_out, counter_1_q[4]);
  not not_3 (not_3_out, counter_1_q[3]);
  and and_1 (and_1_out, counter_1_q[5], not_2_out, not_3_out, not_4_out, not_5_out, not_6_out);
  not not_4 (not_4_out, counter_1_q[2]);
  not not_5 (not_5_out, counter_1_q[1]);
  not not_6 (not_6_out, counter_1_q[0]);
  Multiplexer #(.enable("false"), .width(4)) multiplexer_1 (
    .in0(counter_2_q), .in1(4'b0000), .out(multiplexer_1_out), .sel(Switch));
  not not_7 (not_7_out, and_1_out);
  RAM #(.addrWidth(5), .dataWidth(4)) ram_1 (
    .addr(counter_1_q[4:0]), .we(not_7_out), .oe(not_7_out), .clk(Clk_out), .din(multiplexer_1_out),
    .dout(ram_1_dout));
  Display display_1 (
    .SW_3(ram_1_dout[3]), .SW_2(ram_1_dout[2]), .SW_1(ram_1_dout[1]), .SW_0(ram_1_dout[0]),
    .S0(display_1_s0), .S1(display_1_s1), .S2(display_1_s2), .S3(display_1_s3), .S4(display_1_s4),
    .S5(display_1_s5), .S6(display_1_s6));
  _7_Segment_Display u_7_segment_display_1 (
    .g(display_1_s6), .f(display_1_s5), .a(display_1_s0), .b(display_1_s1), .e(display_1_s4),
    .d(display_1_s3), .c(display_1_s2));  // open: dp
endmodule

module Segment0 (
  input  c_3,
  input  c_2,
  input  c_1,
  input  c_0,
  output Hex0
);

  wire and_1_out, and_2_out, and_3_out, and_4_out, and_5_out, and_6_out, not_1_out, not_2_out, not_3_out,
       not_4_out, not_5_out;

  not not_1 (not_1_out, c_0);
  not not_2 (not_2_out, c_3);
  not not_3 (not_3_out, c_2);
  not not_4 (not_4_out, c_0);
  not not_5 (not_5_out, c_1);
  and and_1 (and_1_out, c_3, not_1_out);
  and and_2 (and_2_out, not_2_out, c_1);
  and and_3 (and_3_out, not_3_out, not_4_out);
  and and_4 (and_4_out, c_1, c_2);
  and and_5 (and_5_out, not_2_out, c_2, c_0);
  and and_6 (and_6_out, c_3, not_3_out, not_5_out);
  or or_1 (Hex0, and_1_out, and_2_out, and_3_out, and_4_out, and_5_out, and_6_out);
endmodule

module Segment1 (
  input  c_3,
  input  c_2,
  input  c_1,
  input  c_0,
  output Hex1
);

  wire and_1_out, and_2_out, and_3_out, and_4_out, and_5_out, not_1_out, not_2_out, not_3_out, not_4_out;

  not not_1 (not_1_out, c_3);
  not not_2 (not_2_out, c_2);
  not not_3 (not_3_out, c_1);
  not not_4 (not_4_out, c_0);
  and and_1 (and_1_out, not_2_out, not_4_out);
  and and_2 (and_2_out, not_1_out, not_2_out);
  and and_3 (and_3_out, not_1_out, not_3_out, not_4_out);
  and and_4 (and_4_out, c_3, not_3_out, c_0);
  and and_5 (and_5_out, not_1_out, c_1, c_0);
  or or_1 (Hex1, and_1_out, and_2_out, and_3_out, and_4_out, and_5_out);
endmodule

module Segment2 (
  input  c_3,
  input  c_2,
  input  c_1,
  input  c_0,
  output Hex2
);

  wire and_1_out, and_2_out, and_3_out, and_4_out, and_5_out, not_1_out, not_2_out, not_3_out;

  not not_1 (not_1_out, c_3);
  not not_2 (not_2_out, c_2);
  not not_3 (not_3_out, c_1);
  and and_1 (and_1_out, not_1_out, not_3_out);
  and and_2 (and_2_out, not_1_out, c_0);
  and and_3 (and_3_out, c_3, not_2_out);
  and and_4 (and_4_out, not_1_out, c_2);
  and and_5 (and_5_out, not_3_out, c_0);
  or or_1 (Hex2, and_1_out, and_2_out, and_3_out, and_4_out, and_5_out);
endmodule

module Segment3 (
  input  c_3,
  input  c_2,
  input  c_1,
  input  c_0,
  output Hex3
);

  wire and_1_out, and_2_out, and_3_out, and_4_out, and_5_out, not_1_out, not_2_out, not_3_out, not_4_out;

  not not_1 (not_1_out, c_3);
  not not_2 (not_2_out, c_2);
  not not_3 (not_3_out, c_1);
  not not_4 (not_4_out, c_0);
  and and_1 (and_1_out, not_1_out, not_2_out, not_4_out);
  and and_2 (and_2_out, c_3, not_3_out, not_4_out);
  and and_3 (and_3_out, c_2, not_3_out, c_0);
  and and_4 (and_4_out, not_2_out, c_1, c_0);
  and and_5 (and_5_out, c_2, c_1, not_4_out);
  or or_1 (Hex3, and_1_out, and_2_out, and_3_out, and_4_out, and_5_out);
endmodule

module Segment4 (
  input  c_3,
  input  c_2,
  input  c_1,
  input  c_0,
  output Hex4
);

  wire and_1_out, and_2_out, and_3_out, and_4_out, not_1_out, not_2_out;

  not not_1 (not_1_out, c_2);
  not not_2 (not_2_out, c_0);
  and and_1 (and_1_out, c_3, c_2);
  and and_2 (and_2_out, c_1, not_2_out);
  and and_3 (and_3_out, not_1_out, not_2_out);
  and and_4 (and_4_out, c_3, c_1);
  or or_1 (Hex4, and_1_out, and_2_out, and_3_out, and_4_out);
endmodule

module Segment5 (
  input  c_3,
  input  c_2,
  input  c_1,
  input  c_0,
  output Hex5
);

  wire and_1_out, and_2_out, and_3_out, and_4_out, and_5_out, not_1_out, not_2_out, not_3_out, not_4_out;

  not not_1 (not_1_out, c_3);
  not not_2 (not_2_out, c_2);
  not not_3 (not_3_out, c_1);
  not not_4 (not_4_out, c_0);
  and and_1 (and_1_out, not_3_out, not_4_out);
  and and_2 (and_2_out, c_3, not_2_out);
  and and_3 (and_3_out, not_1_out, c_2, not_3_out);
  and and_4 (and_4_out, c_3, c_2, c_1);
  and and_5 (and_5_out, c_2, c_1, not_4_out);
  or or_1 (Hex5, and_1_out, and_2_out, and_3_out, and_4_out, and_5_out);
endmodule

module Segment6 (
  input  c_3,
  input  c_2,
  input  c_1,
  input  c_0,
  output Hex6
);

  wire and_1_out, and_2_out, and_3_out, and_4_out, and_5_out, and_6_out, not_1_out, not_2_out, not_3_out,
       not_4_out;

  not not_1 (not_1_out, c_3);
  not not_2 (not_2_out, c_2);
  not not_3 (not_3_out, c_1);
  not not_4 (not_4_out, c_0);
  and and_1 (and_1_out, c_3, not_2_out);
  and and_2 (and_2_out, c_1, not_4_out);
  and and_3 (and_3_out, c_3, c_0);
  and and_4 (and_4_out, c_3, c_1);
  and and_5 (and_5_out, not_1_out, c_2, not_3_out);
  and and_6 (and_6_out, not_1_out, not_2_out, c_1);
  or or_1 (Hex6, and_1_out, and_2_out, and_3_out, and_4_out, and_5_out, and_6_out);
endmodule

module Display (
  input  SW_3,
  input  SW_2,
  input  SW_1,
  input  SW_0,
  output S0,
  output S1,
  output S2,
  output S3,
  output S4,
  output S5,
  output S6
);

  Segment0 Hex0 (.c_3(SW_3), .c_2(SW_2), .c_1(SW_1), .c_0(SW_0), .Hex0(S0));
  Segment1 Hex1 (.c_3(SW_3), .c_2(SW_2), .c_1(SW_1), .c_0(SW_0), .Hex1(S1));
  Segment2 Hex2 (.c_3(SW_3), .c_2(SW_2), .c_1(SW_1), .c_0(SW_0), .Hex2(S2));
  Segment3 Hex3 (.c_3(SW_3), .c_2(SW_2), .c_1(SW_1), .c_0(SW_0), .Hex3(S3));
  Segment4 Hex4 (.c_3(SW_3), .c_2(SW_2), .c_1(SW_1), .c_0(SW_0), .Hex4(S4));
  Segment5 Hex5 (.c_3(SW_3), .c_2(SW_2), .c_1(SW_1), .c_0(SW_0), .Hex5(S5));
  Segment6 Hex6 (.c_3(SW_3), .c_2(SW_2), .c_1(SW_1), .c_0(SW_0), .Hex6(S6));
endmodule
