// Logisim project lab7_part2.circ as structural Verilog: 4 circuits, main circuit main
module main (
  input  Reset,
  input  Enable,
  input  [6:0] Y,
  input  [6:0] X
);

  wire clock_1_out, fsm_1_enable_out;
  wire [6:0] fsm_1_x_out, fsm_1_y_out;
  wire [23:0] fsm_1_color;

  Clock clock_1 (.out(clock_1_out));
  FSM fsm_1 (
    .Enable(Enable), .Clock(clock_1_out), .Reset(Reset), .Y_in(Y), .X_in(X), .clk(clock_1_out),
    .enable_out(fsm_1_enable_out), .Y_out(fsm_1_y_out), .X_out(fsm_1_x_out), .color(fsm_1_color));
  // RGB_Video rgb_video_1: pin names not known; wires that end beside it: Reset, clock_1_out, fsm_1_enable_out, fsm_1_x_out, fsm_1_y_out, fsm_1_color
endmodule

module Datapath (
  input  Enable,
  input  [6:0] Y_in,
  input  Clock,
  input  [6:0] X_in,
  output WriteEnable,
  output [6:0] Y_out,
  output [6:0] X_out,
  output [23:0] color
);

  wire and_1_out, not_1_out;
  wire [3:0] counter_1_q, counter_2_q;
  wire [6:0] bit_extender_1_out, bit_extender_2_out;

  not not_1 (not_1_out, Enable);
  Counter #(.max('hf), .width(4)) counter_1 (
    .clr(not_1_out), .clk(and_1_out), .D(4'b0000), .Q(counter_1_q));  // open: load, up, count, carry
  Counter #(.max('hf), .width(4)) counter_2 (
    .clr(not_1_out), .clk(Clock), .D(4'b0000), .Q(counter_2_q));  // open: load, up, count, carry
  assign bit_extender_1_out = {{3{1'b0}}, counter_1_q};  // Bit_Extender bit_extender_1
  and and_1 (and_1_out, counter_2_q[3], counter_2_q[2], counter_2_q[1], counter_2_q[0]);
  assign bit_extender_2_out = {{3{1'b0}}, counter_2_q};  // Bit_Extender bit_extender_2
  Adder #(.width(7)) adder_1 (.a(Y_in), .b(bit_extender_1_out), .out(Y_out));  // open: cin, cout
  Adder #(.width(7)) adder_2 (.a(bit_extender_2_out), .b(X_in), .out(X_out));  // open: cin, cout

  assign color = 24'hb6ac9f;
  assign WriteEnable = Enable;
endmodule

module FSM (
  input  Enable,
  input  Clock,
  input  Reset,
  input  [6:0] Y_in,
  input  [6:0] X_in,
  input  clk,
  output enable_out,
  output [6:0] Y_out,
  output [6:0] X_out,
  output [23:0] color
);

  wire multiplexer_1_out, register_1_q, state_table_1_enable, state_table_1_next_state;

  state_table state_table_1 (
    .State(multiplexer_1_out), .Enable(state_table_1_enable), .Next_state(state_table_1_next_state));
  Register #(.width(1)) register_1 (
    .D(state_table_1_next_state), .en(Enable), .clk(Clock), .Q(register_1_q), .clr(Reset));
  Multiplexer #(.enable("false")) multiplexer_1 (.in0(1'b0), .in1(register_1_q), .out(multiplexer_1_out), .sel(Enable));
  Datapath datapath_1 (
    .Enable(state_table_1_enable), .Y_in(Y_in), .Clock(clk), .X_in(X_in), .WriteEnable(enable_out),
    .Y_out(Y_out), .X_out(X_out), .color(color));
endmodule

module state_table (
  input  State,
  output Enable,
  output Next_state
);

  wire not_1_out;

  not not_1 (not_1_out, State);
  or or_1 (Next_state, not_1_out, State);

  assign Enable = State;
endmodule
